# Fritzing sketch Sketch (saved by Fritzing 0.9.3b)
breadboards: 1

parts:
  Part1 = Arduino Uno (Rev3)
  Part2 = Bluetooth HC-06 Macho
  ZS-042_RTC1 = ZS-042 RTC Module
  DS1 = DS18B20 1-Wire Temperature Sensor [part_number=DS18B20]
  R1 = Resistor [tolerance=±5% resistance=4.7k package=THT]

nets:
  N1: Part1.A4/SDA, ZS-042_RTC1.SDA
  N2: Part1.A5/SCL, ZS-042_RTC1.SCL
  N3: Part1.D2, Part2.TXD
  N4: Part1.D3_PWM, Part2.RXD
  N5: Part1.D7, DS1.DQ, R1.Pin_1
  VCC: Part1.5V, Part2.VCC, ZS-042_RTC1.VCC, DS1.VDD, R1.Pin_0
  GND: Part1.GND, Part2.GND, ZS-042_RTC1.GND, DS1.GND
